// Logisim project tennis0.3.1.circ as structural Verilog: 4 circuits, main circuit main
module main (
  input  [4:0] in_1,
  input  [4:0] in_2,
  input  [4:0] in_3,
  input  [4:0] in_4
);

  wire [3:0] undriven, undriven_2, undriven_3, undriven_4;
  wire [4:0] videochip8_1_ballx_out, videochip8_1_bally_out, videochip8_1_chipid_out,
       videochip8_1_leftbaty_out, videochip8_1_rightbaty_out, videochip8_2_ballx_out, videochip8_2_bally_out,
       videochip8_2_chipid_out, videochip8_2_leftbaty_out, videochip8_2_rightbaty_out,
       videochip8_3_ballx_out, videochip8_3_bally_out, videochip8_3_chipid_out, videochip8_3_leftbaty_out,
       videochip8_3_rightbaty_out;
  wire [31:0] videochip8_1_columnpattern1, videochip8_1_columnpattern2, videochip8_1_columnpattern3,
       videochip8_1_columnpattern4, videochip8_1_columnpattern5, videochip8_1_columnpattern6,
       videochip8_1_columnpattern7, videochip8_1_columnpattern8, videochip8_2_columnpattern1,
       videochip8_2_columnpattern2, videochip8_2_columnpattern3, videochip8_2_columnpattern4,
       videochip8_2_columnpattern5, videochip8_2_columnpattern6, videochip8_2_columnpattern7,
       videochip8_2_columnpattern8, videochip8_3_columnpattern1, videochip8_3_columnpattern2,
       videochip8_3_columnpattern3, videochip8_3_columnpattern4, videochip8_3_columnpattern5,
       videochip8_3_columnpattern6, videochip8_3_columnpattern7, videochip8_3_columnpattern8,
       videochip8_4_columnpattern1, videochip8_4_columnpattern2, videochip8_4_columnpattern3,
       videochip8_4_columnpattern4, videochip8_4_columnpattern5, videochip8_4_columnpattern6,
       videochip8_4_columnpattern7, videochip8_4_columnpattern8;

  Hex_Digit_Display hex_digit_display_1 (.value(undriven));  // open: dp
  Hex_Digit_Display hex_digit_display_2 (.value(undriven_2));  // open: dp
  DotMatrix #(.matrixcols(32), .matrixrows(32)) dotmatrix_1 (
    .col0(videochip8_1_columnpattern1), .col1(videochip8_1_columnpattern2),
    .col2(videochip8_1_columnpattern3), .col3(videochip8_1_columnpattern4),
    .col4(videochip8_1_columnpattern5), .col5(videochip8_1_columnpattern6),
    .col6(videochip8_1_columnpattern7), .col7(videochip8_1_columnpattern8),
    .col8(videochip8_2_columnpattern1), .col9(videochip8_2_columnpattern2),
    .col10(videochip8_2_columnpattern3), .col11(videochip8_2_columnpattern4),
    .col12(videochip8_2_columnpattern5), .col13(videochip8_2_columnpattern6),
    .col14(videochip8_2_columnpattern7), .col15(videochip8_2_columnpattern8),
    .col16(videochip8_3_columnpattern1), .col17(videochip8_3_columnpattern2),
    .col18(videochip8_3_columnpattern3), .col19(videochip8_3_columnpattern4),
    .col20(videochip8_3_columnpattern5), .col21(videochip8_3_columnpattern6),
    .col22(videochip8_3_columnpattern7), .col23(videochip8_3_columnpattern8),
    .col24(videochip8_4_columnpattern1), .col25(videochip8_4_columnpattern2),
    .col26(videochip8_4_columnpattern3), .col27(videochip8_4_columnpattern4),
    .col28(videochip8_4_columnpattern5), .col29(videochip8_4_columnpattern6),
    .col30(videochip8_4_columnpattern7), .col31(videochip8_4_columnpattern8));
  videochip8 videochip8_1 (
    .chipID({5{1'b0}}), .ballX(in_1), .ballY(in_2), .leftbatY(in_3), .rightbatY(in_4),
    .chipID_out(videochip8_1_chipid_out), .ballX_out(videochip8_1_ballx_out),
    .ballY_out(videochip8_1_bally_out), .leftbatY_out(videochip8_1_leftbaty_out),
    .rightbatY_out(videochip8_1_rightbaty_out), .columnPattern1(videochip8_1_columnpattern1),
    .columnPattern2(videochip8_1_columnpattern2), .columnPattern3(videochip8_1_columnpattern3),
    .columnPattern4(videochip8_1_columnpattern4), .columnPattern5(videochip8_1_columnpattern5),
    .columnPattern6(videochip8_1_columnpattern6), .columnPattern7(videochip8_1_columnpattern7),
    .columnPattern8(videochip8_1_columnpattern8));
  videochip8 videochip8_2 (
    .chipID(videochip8_1_chipid_out), .ballX(videochip8_1_ballx_out), .ballY(videochip8_1_bally_out),
    .leftbatY(videochip8_1_leftbaty_out), .rightbatY(videochip8_1_rightbaty_out),
    .chipID_out(videochip8_2_chipid_out), .ballX_out(videochip8_2_ballx_out),
    .ballY_out(videochip8_2_bally_out), .leftbatY_out(videochip8_2_leftbaty_out),
    .rightbatY_out(videochip8_2_rightbaty_out), .columnPattern1(videochip8_2_columnpattern1),
    .columnPattern2(videochip8_2_columnpattern2), .columnPattern3(videochip8_2_columnpattern3),
    .columnPattern4(videochip8_2_columnpattern4), .columnPattern5(videochip8_2_columnpattern5),
    .columnPattern6(videochip8_2_columnpattern6), .columnPattern7(videochip8_2_columnpattern7),
    .columnPattern8(videochip8_2_columnpattern8));
  videochip8 videochip8_3 (
    .chipID(videochip8_2_chipid_out), .ballX(videochip8_2_ballx_out), .ballY(videochip8_2_bally_out),
    .leftbatY(videochip8_2_leftbaty_out), .rightbatY(videochip8_2_rightbaty_out),
    .chipID_out(videochip8_3_chipid_out), .ballX_out(videochip8_3_ballx_out),
    .ballY_out(videochip8_3_bally_out), .leftbatY_out(videochip8_3_leftbaty_out),
    .rightbatY_out(videochip8_3_rightbaty_out), .columnPattern1(videochip8_3_columnpattern1),
    .columnPattern2(videochip8_3_columnpattern2), .columnPattern3(videochip8_3_columnpattern3),
    .columnPattern4(videochip8_3_columnpattern4), .columnPattern5(videochip8_3_columnpattern5),
    .columnPattern6(videochip8_3_columnpattern6), .columnPattern7(videochip8_3_columnpattern7),
    .columnPattern8(videochip8_3_columnpattern8));
  videochip8 videochip8_4 (
    .chipID(videochip8_3_chipid_out), .ballX(videochip8_3_ballx_out), .ballY(videochip8_3_bally_out),
    .leftbatY(videochip8_3_leftbaty_out), .rightbatY(videochip8_3_rightbaty_out),
    .columnPattern1(videochip8_4_columnpattern1), .columnPattern2(videochip8_4_columnpattern2),
    .columnPattern3(videochip8_4_columnpattern3), .columnPattern4(videochip8_4_columnpattern4),
    .columnPattern5(videochip8_4_columnpattern5), .columnPattern6(videochip8_4_columnpattern6),
    .columnPattern7(videochip8_4_columnpattern7), .columnPattern8(videochip8_4_columnpattern8));  // open: chipID_out, ballX_out, ballY_out, leftbatY_out, rightbatY_out
  Hex_Digit_Display hex_digit_display_3 (.value(undriven_3));  // open: dp
  Hex_Digit_Display hex_digit_display_4 (.value(undriven_4));  // open: dp
endmodule

module videochip8 (
  input  [4:0] chipID,
  input  [4:0] ballX,
  input  [4:0] ballY,
  input  [4:0] leftbatY,
  input  [4:0] rightbatY,
  output [31:0] columnPattern1,
  output [31:0] columnPattern3,
  output [31:0] columnPattern5,
  output [31:0] columnPattern7,
  output [31:0] columnPattern2,
  output [31:0] columnPattern4,
  output [31:0] columnPattern6,
  output [31:0] columnPattern8,
  output [4:0] chipID_out,
  output [4:0] ballX_out,
  output [4:0] ballY_out,
  output [4:0] leftbatY_out,
  output [4:0] rightbatY_out
);

  wire [4:0] videochip1_1_ballx_out, videochip1_1_bally_out, videochip1_1_chipid_out,
       videochip1_1_leftbaty_out, videochip1_1_rightbaty_out, videochip1_2_ballx_out, videochip1_2_bally_out,
       videochip1_2_chipid_out, videochip1_2_leftbaty_out, videochip1_2_rightbaty_out,
       videochip1_3_ballx_out, videochip1_3_bally_out, videochip1_3_chipid_out, videochip1_3_leftbaty_out,
       videochip1_3_rightbaty_out, videochip1_4_ballx_out, videochip1_4_bally_out, videochip1_4_chipid_out,
       videochip1_4_leftbaty_out, videochip1_4_rightbaty_out, videochip1_5_ballx_out, videochip1_5_bally_out,
       videochip1_5_chipid_out, videochip1_5_leftbaty_out, videochip1_5_rightbaty_out,
       videochip1_6_ballx_out, videochip1_6_bally_out, videochip1_6_chipid_out, videochip1_6_leftbaty_out,
       videochip1_6_rightbaty_out, videochip1_7_ballx_out, videochip1_7_bally_out, videochip1_7_chipid_out,
       videochip1_7_leftbaty_out, videochip1_7_rightbaty_out;

  videochip1 videochip1_1 (
    .chipID(chipID), .ballX(ballX), .rightbatY(rightbatY), .columnPattern(columnPattern1),
    .chipID_out(videochip1_1_chipid_out), .rightbatY_out(videochip1_1_rightbaty_out),
    .ballX_out(videochip1_1_ballx_out), .ballY(ballY), .ballY_out(videochip1_1_bally_out),
    .leftbatY(leftbatY), .leftbatY_out(videochip1_1_leftbaty_out));
  videochip1 videochip1_2 (
    .chipID(videochip1_1_chipid_out), .ballX(videochip1_1_ballx_out), .rightbatY(videochip1_1_rightbaty_out),
    .columnPattern(columnPattern2), .chipID_out(videochip1_2_chipid_out),
    .rightbatY_out(videochip1_2_rightbaty_out), .ballX_out(videochip1_2_ballx_out),
    .ballY(videochip1_1_bally_out), .ballY_out(videochip1_2_bally_out), .leftbatY(videochip1_1_leftbaty_out),
    .leftbatY_out(videochip1_2_leftbaty_out));
  videochip1 videochip1_3 (
    .chipID(videochip1_2_chipid_out), .ballX(videochip1_2_ballx_out), .rightbatY(videochip1_2_rightbaty_out),
    .columnPattern(columnPattern3), .chipID_out(videochip1_3_chipid_out),
    .rightbatY_out(videochip1_3_rightbaty_out), .ballX_out(videochip1_3_ballx_out),
    .ballY(videochip1_2_bally_out), .ballY_out(videochip1_3_bally_out), .leftbatY(videochip1_2_leftbaty_out),
    .leftbatY_out(videochip1_3_leftbaty_out));
  videochip1 videochip1_4 (
    .chipID(videochip1_3_chipid_out), .ballX(videochip1_3_ballx_out), .rightbatY(videochip1_3_rightbaty_out),
    .columnPattern(columnPattern4), .chipID_out(videochip1_4_chipid_out),
    .rightbatY_out(videochip1_4_rightbaty_out), .ballX_out(videochip1_4_ballx_out),
    .ballY(videochip1_3_bally_out), .ballY_out(videochip1_4_bally_out), .leftbatY(videochip1_3_leftbaty_out),
    .leftbatY_out(videochip1_4_leftbaty_out));
  videochip1 videochip1_5 (
    .chipID(videochip1_4_chipid_out), .ballX(videochip1_4_ballx_out), .rightbatY(videochip1_4_rightbaty_out),
    .columnPattern(columnPattern5), .chipID_out(videochip1_5_chipid_out),
    .rightbatY_out(videochip1_5_rightbaty_out), .ballX_out(videochip1_5_ballx_out),
    .ballY(videochip1_4_bally_out), .ballY_out(videochip1_5_bally_out), .leftbatY(videochip1_4_leftbaty_out),
    .leftbatY_out(videochip1_5_leftbaty_out));
  videochip1 videochip1_6 (
    .chipID(videochip1_5_chipid_out), .ballX(videochip1_5_ballx_out), .rightbatY(videochip1_5_rightbaty_out),
    .columnPattern(columnPattern6), .chipID_out(videochip1_6_chipid_out),
    .rightbatY_out(videochip1_6_rightbaty_out), .ballX_out(videochip1_6_ballx_out),
    .ballY(videochip1_5_bally_out), .ballY_out(videochip1_6_bally_out), .leftbatY(videochip1_5_leftbaty_out),
    .leftbatY_out(videochip1_6_leftbaty_out));
  videochip1 videochip1_7 (
    .chipID(videochip1_6_chipid_out), .ballX(videochip1_6_ballx_out), .rightbatY(videochip1_6_rightbaty_out),
    .columnPattern(columnPattern7), .chipID_out(videochip1_7_chipid_out),
    .rightbatY_out(videochip1_7_rightbaty_out), .ballX_out(videochip1_7_ballx_out),
    .ballY(videochip1_6_bally_out), .ballY_out(videochip1_7_bally_out), .leftbatY(videochip1_6_leftbaty_out),
    .leftbatY_out(videochip1_7_leftbaty_out));
  videochip1 videochip1_8 (
    .chipID(videochip1_7_chipid_out), .ballX(videochip1_7_ballx_out), .rightbatY(videochip1_7_rightbaty_out),
    .columnPattern(columnPattern8), .chipID_out(chipID_out), .rightbatY_out(rightbatY_out),
    .ballX_out(ballX_out), .ballY(videochip1_7_bally_out), .ballY_out(ballY_out),
    .leftbatY(videochip1_7_leftbaty_out), .leftbatY_out(leftbatY_out));
endmodule

module videochip1 (
  input  [4:0] chipID,
  input  [4:0] ballX,
  input  [4:0] ballY,
  input  [4:0] leftbatY,
  input  [4:0] rightbatY,
  output [4:0] chipID_out,
  output [4:0] ballX_out,
  output [4:0] ballY_out,
  output [4:0] leftbatY_out,
  output [31:0] columnPattern,
  output [4:0] rightbatY_out
);

  wire comparator_1_eq, comparator_2_eq, comparator_3_gt, comparator_4_gt, comparator_5_eq;
  wire [4:0] adder_2_out, adder_3_out, adder_4_out, adder_5_out, multiplexer_1_out, multiplexer_2_out;
  wire [31:0] decoder_1_out0, decoder_2_out0, decoder_3_out0, decoder_4_out0, decoder_5_out0, decoder_6_out0,
       decoder_7_out0, multiplexer_3_out, or_1_out, or_2_out;

  Comparator #(.width(5)) comparator_1 (.a(chipID), .b(5'b00011), .eq(comparator_1_eq));  // open: gt, lt
  Comparator #(.width(5)) comparator_2 (.a(chipID), .b(5'b11100), .eq(comparator_2_eq));  // open: gt, lt
  Adder #(.width(5)) adder_1 (.a(chipID), .b(5'b00001), .out(chipID_out));  // open: cin, cout
  Comparator #(.width(5), .mode("unsigned")) comparator_3 (
    .a(5'b11101), .b(leftbatY), .gt(comparator_3_gt));  // open: eq, lt
  Comparator #(.width(5), .mode("unsigned")) comparator_4 (
    .a(5'b11101), .b(rightbatY), .gt(comparator_4_gt));  // open: eq, lt
  Comparator #(.width(5)) comparator_5 (.a(chipID), .b(ballX), .eq(comparator_5_eq));  // open: gt, lt
  Multiplexer #(.width(5)) multiplexer_1 (
    .in0(5'b11101), .in1(leftbatY), .out(multiplexer_1_out), .sel(comparator_3_gt));  // open: en
  Decoder #(.select(5), .disabled(0)) decoder_1 (
    .out0(decoder_1_out0[0]), .out1(decoder_1_out0[1]), .out2(decoder_1_out0[2]), .out3(decoder_1_out0[3]),
    .out4(decoder_1_out0[4]), .out5(decoder_1_out0[5]), .out6(decoder_1_out0[6]), .out7(decoder_1_out0[7]),
    .out8(decoder_1_out0[8]), .out9(decoder_1_out0[9]), .out10(decoder_1_out0[10]),
    .out11(decoder_1_out0[11]), .out12(decoder_1_out0[12]), .out13(decoder_1_out0[13]),
    .out14(decoder_1_out0[14]), .out15(decoder_1_out0[15]), .out16(decoder_1_out0[16]),
    .out17(decoder_1_out0[17]), .out18(decoder_1_out0[18]), .out19(decoder_1_out0[19]),
    .out20(decoder_1_out0[20]), .out21(decoder_1_out0[21]), .out22(decoder_1_out0[22]),
    .out23(decoder_1_out0[23]), .out24(decoder_1_out0[24]), .out25(decoder_1_out0[25]),
    .out26(decoder_1_out0[26]), .out27(decoder_1_out0[27]), .out28(decoder_1_out0[28]),
    .out29(decoder_1_out0[29]), .out30(decoder_1_out0[30]), .out31(decoder_1_out0[31]),
    .sel(multiplexer_1_out), .en(comparator_1_eq));
  Decoder #(.select(5), .disabled(0)) decoder_2 (
    .out0(decoder_2_out0[0]), .out1(decoder_2_out0[1]), .out2(decoder_2_out0[2]), .out3(decoder_2_out0[3]),
    .out4(decoder_2_out0[4]), .out5(decoder_2_out0[5]), .out6(decoder_2_out0[6]), .out7(decoder_2_out0[7]),
    .out8(decoder_2_out0[8]), .out9(decoder_2_out0[9]), .out10(decoder_2_out0[10]),
    .out11(decoder_2_out0[11]), .out12(decoder_2_out0[12]), .out13(decoder_2_out0[13]),
    .out14(decoder_2_out0[14]), .out15(decoder_2_out0[15]), .out16(decoder_2_out0[16]),
    .out17(decoder_2_out0[17]), .out18(decoder_2_out0[18]), .out19(decoder_2_out0[19]),
    .out20(decoder_2_out0[20]), .out21(decoder_2_out0[21]), .out22(decoder_2_out0[22]),
    .out23(decoder_2_out0[23]), .out24(decoder_2_out0[24]), .out25(decoder_2_out0[25]),
    .out26(decoder_2_out0[26]), .out27(decoder_2_out0[27]), .out28(decoder_2_out0[28]),
    .out29(decoder_2_out0[29]), .out30(decoder_2_out0[30]), .out31(decoder_2_out0[31]),
    .sel(multiplexer_2_out), .en(comparator_2_eq));
  Multiplexer #(.width(5)) multiplexer_2 (
    .in0(5'b11101), .in1(rightbatY), .out(multiplexer_2_out), .sel(comparator_4_gt));  // open: en
  Adder #(.width(5)) adder_2 (.a(multiplexer_1_out), .b(5'b00001), .out(adder_2_out));  // open: cin, cout
  Adder #(.width(5)) adder_3 (.a(multiplexer_2_out), .b(5'b00001), .out(adder_3_out));  // open: cin, cout
  assign or_1_out = decoder_1_out0 | decoder_3_out0 | decoder_5_out0;  // OR_Gate or_1, 32 bits wide
  Decoder #(.select(5), .disabled(0)) decoder_3 (
    .out0(decoder_3_out0[0]), .out1(decoder_3_out0[1]), .out2(decoder_3_out0[2]), .out3(decoder_3_out0[3]),
    .out4(decoder_3_out0[4]), .out5(decoder_3_out0[5]), .out6(decoder_3_out0[6]), .out7(decoder_3_out0[7]),
    .out8(decoder_3_out0[8]), .out9(decoder_3_out0[9]), .out10(decoder_3_out0[10]),
    .out11(decoder_3_out0[11]), .out12(decoder_3_out0[12]), .out13(decoder_3_out0[13]),
    .out14(decoder_3_out0[14]), .out15(decoder_3_out0[15]), .out16(decoder_3_out0[16]),
    .out17(decoder_3_out0[17]), .out18(decoder_3_out0[18]), .out19(decoder_3_out0[19]),
    .out20(decoder_3_out0[20]), .out21(decoder_3_out0[21]), .out22(decoder_3_out0[22]),
    .out23(decoder_3_out0[23]), .out24(decoder_3_out0[24]), .out25(decoder_3_out0[25]),
    .out26(decoder_3_out0[26]), .out27(decoder_3_out0[27]), .out28(decoder_3_out0[28]),
    .out29(decoder_3_out0[29]), .out30(decoder_3_out0[30]), .out31(decoder_3_out0[31]), .sel(adder_2_out),
    .en(comparator_1_eq));
  assign or_2_out = decoder_2_out0 | decoder_4_out0 | decoder_6_out0;  // OR_Gate or_2, 32 bits wide
  Decoder #(.select(5), .disabled(0)) decoder_4 (
    .out0(decoder_4_out0[0]), .out1(decoder_4_out0[1]), .out2(decoder_4_out0[2]), .out3(decoder_4_out0[3]),
    .out4(decoder_4_out0[4]), .out5(decoder_4_out0[5]), .out6(decoder_4_out0[6]), .out7(decoder_4_out0[7]),
    .out8(decoder_4_out0[8]), .out9(decoder_4_out0[9]), .out10(decoder_4_out0[10]),
    .out11(decoder_4_out0[11]), .out12(decoder_4_out0[12]), .out13(decoder_4_out0[13]),
    .out14(decoder_4_out0[14]), .out15(decoder_4_out0[15]), .out16(decoder_4_out0[16]),
    .out17(decoder_4_out0[17]), .out18(decoder_4_out0[18]), .out19(decoder_4_out0[19]),
    .out20(decoder_4_out0[20]), .out21(decoder_4_out0[21]), .out22(decoder_4_out0[22]),
    .out23(decoder_4_out0[23]), .out24(decoder_4_out0[24]), .out25(decoder_4_out0[25]),
    .out26(decoder_4_out0[26]), .out27(decoder_4_out0[27]), .out28(decoder_4_out0[28]),
    .out29(decoder_4_out0[29]), .out30(decoder_4_out0[30]), .out31(decoder_4_out0[31]), .sel(adder_3_out),
    .en(comparator_2_eq));
  Decoder #(.select(5), .disabled(0)) decoder_5 (
    .out0(decoder_5_out0[0]), .out1(decoder_5_out0[1]), .out2(decoder_5_out0[2]), .out3(decoder_5_out0[3]),
    .out4(decoder_5_out0[4]), .out5(decoder_5_out0[5]), .out6(decoder_5_out0[6]), .out7(decoder_5_out0[7]),
    .out8(decoder_5_out0[8]), .out9(decoder_5_out0[9]), .out10(decoder_5_out0[10]),
    .out11(decoder_5_out0[11]), .out12(decoder_5_out0[12]), .out13(decoder_5_out0[13]),
    .out14(decoder_5_out0[14]), .out15(decoder_5_out0[15]), .out16(decoder_5_out0[16]),
    .out17(decoder_5_out0[17]), .out18(decoder_5_out0[18]), .out19(decoder_5_out0[19]),
    .out20(decoder_5_out0[20]), .out21(decoder_5_out0[21]), .out22(decoder_5_out0[22]),
    .out23(decoder_5_out0[23]), .out24(decoder_5_out0[24]), .out25(decoder_5_out0[25]),
    .out26(decoder_5_out0[26]), .out27(decoder_5_out0[27]), .out28(decoder_5_out0[28]),
    .out29(decoder_5_out0[29]), .out30(decoder_5_out0[30]), .out31(decoder_5_out0[31]), .sel(adder_4_out),
    .en(comparator_1_eq));
  Adder #(.width(5)) adder_4 (.a(adder_2_out), .b(5'b00001), .out(adder_4_out));  // open: cin, cout
  Decoder #(.select(5), .disabled(0)) decoder_6 (
    .out0(decoder_6_out0[0]), .out1(decoder_6_out0[1]), .out2(decoder_6_out0[2]), .out3(decoder_6_out0[3]),
    .out4(decoder_6_out0[4]), .out5(decoder_6_out0[5]), .out6(decoder_6_out0[6]), .out7(decoder_6_out0[7]),
    .out8(decoder_6_out0[8]), .out9(decoder_6_out0[9]), .out10(decoder_6_out0[10]),
    .out11(decoder_6_out0[11]), .out12(decoder_6_out0[12]), .out13(decoder_6_out0[13]),
    .out14(decoder_6_out0[14]), .out15(decoder_6_out0[15]), .out16(decoder_6_out0[16]),
    .out17(decoder_6_out0[17]), .out18(decoder_6_out0[18]), .out19(decoder_6_out0[19]),
    .out20(decoder_6_out0[20]), .out21(decoder_6_out0[21]), .out22(decoder_6_out0[22]),
    .out23(decoder_6_out0[23]), .out24(decoder_6_out0[24]), .out25(decoder_6_out0[25]),
    .out26(decoder_6_out0[26]), .out27(decoder_6_out0[27]), .out28(decoder_6_out0[28]),
    .out29(decoder_6_out0[29]), .out30(decoder_6_out0[30]), .out31(decoder_6_out0[31]), .sel(adder_5_out),
    .en(comparator_2_eq));
  Adder #(.width(5)) adder_5 (.a(adder_3_out), .b(5'b00001), .out(adder_5_out));  // open: cin, cout
  Decoder #(.select(5), .enable("false")) decoder_7 (
    .out0(decoder_7_out0[0]), .out1(decoder_7_out0[1]), .out2(decoder_7_out0[2]), .out3(decoder_7_out0[3]),
    .out4(decoder_7_out0[4]), .out5(decoder_7_out0[5]), .out6(decoder_7_out0[6]), .out7(decoder_7_out0[7]),
    .out8(decoder_7_out0[8]), .out9(decoder_7_out0[9]), .out10(decoder_7_out0[10]),
    .out11(decoder_7_out0[11]), .out12(decoder_7_out0[12]), .out13(decoder_7_out0[13]),
    .out14(decoder_7_out0[14]), .out15(decoder_7_out0[15]), .out16(decoder_7_out0[16]),
    .out17(decoder_7_out0[17]), .out18(decoder_7_out0[18]), .out19(decoder_7_out0[19]),
    .out20(decoder_7_out0[20]), .out21(decoder_7_out0[21]), .out22(decoder_7_out0[22]),
    .out23(decoder_7_out0[23]), .out24(decoder_7_out0[24]), .out25(decoder_7_out0[25]),
    .out26(decoder_7_out0[26]), .out27(decoder_7_out0[27]), .out28(decoder_7_out0[28]),
    .out29(decoder_7_out0[29]), .out30(decoder_7_out0[30]), .out31(decoder_7_out0[31]), .sel(ballY));
  Multiplexer #(.width(32)) multiplexer_3 (
    .in0({32{1'b0}}), .in1(decoder_7_out0), .out(multiplexer_3_out), .sel(comparator_5_eq));  // open: en
  assign columnPattern = multiplexer_3_out | or_1_out | or_2_out;  // OR_Gate or_3, 32 bits wide

  assign ballX_out = ballX;
  assign ballY_out = ballY;
  assign leftbatY_out = leftbatY;
  assign rightbatY_out = rightbatY;
endmodule

module controller (
  input  [7:0] rightbatY_CMD_8,
  input  [4:0] leftbatY,
  input  reset,
  input  tick,
  output [4:0] chipID,
  output [4:0] leftbatY_out,
  output [4:0] rightbatY_out,
  output [7:0] scorePerson,
  output [7:0] scoreRobot,
  output [4:0] ballX_out,
  output [7:0] ballX_CDM_8,
  output [4:0] ballY_out,
  output [7:0] ballY_CDM_8,
  output [7:0] speed_CDM_8
);

  wire comparator_1_gt, not_1_out;
  wire [2:0] multiplexer_5_out, multiplexer_6_out;
  wire [4:0] rightbatY;
  wire [7:0] multiplexer_1_out, multiplexer_2_out, multiplexer_3_out, multiplexer_4_out;

  // Probe on rightbatY_CMD_8
  not not_1 (not_1_out, comparator_1_gt);
  Comparator #(.width(5), .mode("unsigned")) comparator_1 (
    .a(ballX_CDM_8[7:3]), .b(5'b01111), .gt(comparator_1_gt));  // open: eq, lt
  Register #(.width(5)) register_1 (.D(rightbatY_CMD_8[4:0]), .en(not_1_out), .Q(rightbatY), .clk(tick));  // open: clr
  // Probe on leftbatY
  Multiplexer #(.width(8), .enable("false")) multiplexer_1 (
    .in0(scorePerson), .in1({8{1'b0}}), .out(multiplexer_1_out), .sel(reset));
  Multiplexer #(.width(8), .enable("false")) multiplexer_2 (
    .in0(scoreRobot), .in1({8{1'b0}}), .out(multiplexer_2_out), .sel(reset));
  Multiplexer #(.width(8), .enable("false")) multiplexer_3 (
    .in0(ballX_CDM_8), .in1(8'h80), .out(multiplexer_3_out), .sel(reset));
  Multiplexer #(.width(8), .enable("false")) multiplexer_4 (
    .in0(ballY_CDM_8), .in1(8'h80), .out(multiplexer_4_out), .sel(reset));
  Multiplexer #(.width(3), .enable("false")) multiplexer_5 (
    .in0(speed_CDM_8[2:0]), .in1(3'b100), .out(multiplexer_5_out), .sel(reset));
  Multiplexer #(.width(3), .enable("false")) multiplexer_6 (
    .in0(speed_CDM_8[5:3]), .in1(3'b100), .out(multiplexer_6_out), .sel(reset));
  Register #(.trigger("falling")) register_2 (
    .D(multiplexer_1_out), .en(1'b1), .Q(scorePerson), .clk(tick));  // open: clr
  Register #(.trigger("falling")) register_3 (
    .D(multiplexer_2_out), .en(1'b1), .Q(scoreRobot), .clk(tick));  // open: clr
  // Probe on ballX_CDM_8
  Register #(.trigger("falling")) register_4 (
    .D(multiplexer_3_out), .en(1'b1), .Q(ballX_CDM_8), .clk(tick));  // open: clr
  // Probe on ballY_CDM_8
  Register #(.trigger("falling")) register_5 (
    .D(multiplexer_4_out), .en(1'b1), .Q(ballY_CDM_8), .clk(tick));  // open: clr
  // Probe on speed_CDM_8[2:0]
  Register #(.width(3), .trigger("falling")) register_6 (
    .D(multiplexer_5_out), .en(1'b1), .Q(speed_CDM_8[2:0]), .clk(tick));  // open: clr
  // Probe on speed_CDM_8[5:3]
  Register #(.width(3), .trigger("falling")) register_7 (
    .D(multiplexer_6_out), .en(1'b1), .Q(speed_CDM_8[5:3]), .clk(tick));  // open: clr

  assign ballX_out = ballX_CDM_8[7:3];
  assign ballY_out = ballY_CDM_8[7:3];
  assign chipID = {5{1'b0}};
  assign leftbatY_out = leftbatY;
  assign rightbatY_out = rightbatY_CMD_8[4:0];
  assign speed_CDM_8[7:6] = 2'b00;

  // Other names for the same wires on the sheet: ballX[4:0] = ballX_CDM_8[7:3]; ballY[4:0] = ballY_CDM_8[7:3]
endmodule
