// Logisim project tennis1.0.1.circ as structural Verilog: 6 circuits, main circuit main
module main (
  input  in_1
);

  wire and_1_out, clock_1_out, R_out;
  wire [3:0] calcscore_1_ones, calcscore_1_tens, calcscore_2_ones, calcscore_2_tens;
  wire [4:0] controller_1_ballx_out, controller_1_bally_out, controller_1_chipid, controller_1_leftbaty_out,
       controller_1_rightbaty_out, joystick_1_y, not_1_out, videochip8_1_ballx_out, videochip8_1_bally_out,
       videochip8_1_chipid_out, videochip8_1_leftbaty_out, videochip8_1_rightbaty_out,
       videochip8_2_ballx_out, videochip8_2_bally_out, videochip8_2_chipid_out, videochip8_2_leftbaty_out,
       videochip8_2_rightbaty_out, videochip8_3_ballx_out, videochip8_3_bally_out, videochip8_3_chipid_out,
       videochip8_3_leftbaty_out, videochip8_3_rightbaty_out;
  wire [7:0] controller_1_ballx_cdm_8, controller_1_bally_cdm_8, controller_1_speed_cdm_8,
       processor_1_rightbaty, scorePerson, scoreRobot;
  wire [31:0] videochip8_1_columnpattern1, videochip8_1_columnpattern2, videochip8_1_columnpattern3,
       videochip8_1_columnpattern4, videochip8_1_columnpattern5, videochip8_1_columnpattern6,
       videochip8_1_columnpattern7, videochip8_1_columnpattern8, videochip8_2_columnpattern1,
       videochip8_2_columnpattern2, videochip8_2_columnpattern3, videochip8_2_columnpattern4,
       videochip8_2_columnpattern5, videochip8_2_columnpattern6, videochip8_2_columnpattern7,
       videochip8_2_columnpattern8, videochip8_3_columnpattern1, videochip8_3_columnpattern2,
       videochip8_3_columnpattern3, videochip8_3_columnpattern4, videochip8_3_columnpattern5,
       videochip8_3_columnpattern6, videochip8_3_columnpattern7, videochip8_3_columnpattern8,
       videochip8_4_columnpattern1, videochip8_4_columnpattern2, videochip8_4_columnpattern3,
       videochip8_4_columnpattern4, videochip8_4_columnpattern5, videochip8_4_columnpattern6,
       videochip8_4_columnpattern7, videochip8_4_columnpattern8;

  processor processor_1 (
    .rightbatY(processor_1_rightbaty), .ballX(controller_1_ballx_cdm_8), .ballY(controller_1_bally_cdm_8),
    .speed(controller_1_speed_cdm_8));
  and and_1 (and_1_out, in_1, clock_1_out);
  Clock #(.highDuration(15), .lowDuration(15)) clock_1 (.out(clock_1_out));
  Button R (.out(R_out));
  Hex_Digit_Display hex_digit_display_1 (.value(calcscore_1_tens));  // open: dp
  calcScore calcscore_1 (.in(scorePerson), .tens(calcscore_1_tens), .ones(calcscore_1_ones));
  Joystick #(.bits(5)) joystick_1 (.y(joystick_1_y));  // open: x
  assign not_1_out = ~joystick_1_y;  // NOT_Gate not_1, 5 bits wide
  Hex_Digit_Display hex_digit_display_2 (.value(calcscore_1_ones));  // open: dp
  DotMatrix #(.matrixcols(32), .matrixrows(32)) dotmatrix_1 (
    .col0(videochip8_1_columnpattern1), .col1(videochip8_1_columnpattern2),
    .col2(videochip8_1_columnpattern3), .col3(videochip8_1_columnpattern4),
    .col4(videochip8_1_columnpattern5), .col5(videochip8_1_columnpattern6),
    .col6(videochip8_1_columnpattern7), .col7(videochip8_1_columnpattern8),
    .col8(videochip8_2_columnpattern1), .col9(videochip8_2_columnpattern2),
    .col10(videochip8_2_columnpattern3), .col11(videochip8_2_columnpattern4),
    .col12(videochip8_2_columnpattern5), .col13(videochip8_2_columnpattern6),
    .col14(videochip8_2_columnpattern7), .col15(videochip8_2_columnpattern8),
    .col16(videochip8_3_columnpattern1), .col17(videochip8_3_columnpattern2),
    .col18(videochip8_3_columnpattern3), .col19(videochip8_3_columnpattern4),
    .col20(videochip8_3_columnpattern5), .col21(videochip8_3_columnpattern6),
    .col22(videochip8_3_columnpattern7), .col23(videochip8_3_columnpattern8),
    .col24(videochip8_4_columnpattern1), .col25(videochip8_4_columnpattern2),
    .col26(videochip8_4_columnpattern3), .col27(videochip8_4_columnpattern4),
    .col28(videochip8_4_columnpattern5), .col29(videochip8_4_columnpattern6),
    .col30(videochip8_4_columnpattern7), .col31(videochip8_4_columnpattern8));
  controller controller_1 (
    .leftbatY(not_1_out), .rightbatY_CMD_8(processor_1_rightbaty), .leftbatY_out(controller_1_leftbaty_out),
    .rightbatY_out(controller_1_rightbaty_out), .scorePerson(scorePerson), .scoreRobot(scoreRobot),
    .ballX_CDM_8(controller_1_ballx_cdm_8), .ballY_CDM_8(controller_1_bally_cdm_8),
    .speed_CDM_8(controller_1_speed_cdm_8), .chipID(controller_1_chipid), .ballX_out(controller_1_ballx_out),
    .ballY_out(controller_1_bally_out), .reset(R_out), .tick(and_1_out));
  videochip8 videochip8_1 (
    .chipID(controller_1_chipid), .ballX(controller_1_ballx_out), .ballY(controller_1_bally_out),
    .leftbatY(controller_1_leftbaty_out), .rightbatY(controller_1_rightbaty_out),
    .chipID_out(videochip8_1_chipid_out), .ballX_out(videochip8_1_ballx_out),
    .ballY_out(videochip8_1_bally_out), .leftbatY_out(videochip8_1_leftbaty_out),
    .rightbatY_out(videochip8_1_rightbaty_out), .columnPattern1(videochip8_1_columnpattern1),
    .columnPattern2(videochip8_1_columnpattern2), .columnPattern3(videochip8_1_columnpattern3),
    .columnPattern4(videochip8_1_columnpattern4), .columnPattern5(videochip8_1_columnpattern5),
    .columnPattern6(videochip8_1_columnpattern6), .columnPattern7(videochip8_1_columnpattern7),
    .columnPattern8(videochip8_1_columnpattern8));
  videochip8 videochip8_2 (
    .chipID(videochip8_1_chipid_out), .ballX(videochip8_1_ballx_out), .ballY(videochip8_1_bally_out),
    .leftbatY(videochip8_1_leftbaty_out), .rightbatY(videochip8_1_rightbaty_out),
    .chipID_out(videochip8_2_chipid_out), .ballX_out(videochip8_2_ballx_out),
    .ballY_out(videochip8_2_bally_out), .leftbatY_out(videochip8_2_leftbaty_out),
    .rightbatY_out(videochip8_2_rightbaty_out), .columnPattern1(videochip8_2_columnpattern1),
    .columnPattern2(videochip8_2_columnpattern2), .columnPattern3(videochip8_2_columnpattern3),
    .columnPattern4(videochip8_2_columnpattern4), .columnPattern5(videochip8_2_columnpattern5),
    .columnPattern6(videochip8_2_columnpattern6), .columnPattern7(videochip8_2_columnpattern7),
    .columnPattern8(videochip8_2_columnpattern8));
  videochip8 videochip8_3 (
    .chipID(videochip8_2_chipid_out), .ballX(videochip8_2_ballx_out), .ballY(videochip8_2_bally_out),
    .leftbatY(videochip8_2_leftbaty_out), .rightbatY(videochip8_2_rightbaty_out),
    .chipID_out(videochip8_3_chipid_out), .ballX_out(videochip8_3_ballx_out),
    .ballY_out(videochip8_3_bally_out), .leftbatY_out(videochip8_3_leftbaty_out),
    .rightbatY_out(videochip8_3_rightbaty_out), .columnPattern1(videochip8_3_columnpattern1),
    .columnPattern2(videochip8_3_columnpattern2), .columnPattern3(videochip8_3_columnpattern3),
    .columnPattern4(videochip8_3_columnpattern4), .columnPattern5(videochip8_3_columnpattern5),
    .columnPattern6(videochip8_3_columnpattern6), .columnPattern7(videochip8_3_columnpattern7),
    .columnPattern8(videochip8_3_columnpattern8));
  videochip8 videochip8_4 (
    .chipID(videochip8_3_chipid_out), .ballX(videochip8_3_ballx_out), .ballY(videochip8_3_bally_out),
    .leftbatY(videochip8_3_leftbaty_out), .rightbatY(videochip8_3_rightbaty_out),
    .columnPattern1(videochip8_4_columnpattern1), .columnPattern2(videochip8_4_columnpattern2),
    .columnPattern3(videochip8_4_columnpattern3), .columnPattern4(videochip8_4_columnpattern4),
    .columnPattern5(videochip8_4_columnpattern5), .columnPattern6(videochip8_4_columnpattern6),
    .columnPattern7(videochip8_4_columnpattern7), .columnPattern8(videochip8_4_columnpattern8));  // open: chipID_out, ballX_out, ballY_out, leftbatY_out, rightbatY_out
  Hex_Digit_Display hex_digit_display_3 (.value(calcscore_2_ones));  // open: dp
  calcScore calcscore_2 (.in(scoreRobot), .tens(calcscore_2_tens), .ones(calcscore_2_ones));
  Hex_Digit_Display hex_digit_display_4 (.value(calcscore_2_tens));  // open: dp
endmodule

module videochip8 (
  input  [4:0] chipID,
  input  [4:0] ballX,
  input  [4:0] ballY,
  input  [4:0] leftbatY,
  input  [4:0] rightbatY,
  output [31:0] columnPattern1,
  output [31:0] columnPattern3,
  output [31:0] columnPattern5,
  output [31:0] columnPattern7,
  output [31:0] columnPattern2,
  output [31:0] columnPattern4,
  output [31:0] columnPattern6,
  output [31:0] columnPattern8,
  output [4:0] chipID_out,
  output [4:0] ballX_out,
  output [4:0] ballY_out,
  output [4:0] leftbatY_out,
  output [4:0] rightbatY_out
);

  wire [4:0] videochip1_1_ballx_out, videochip1_1_bally_out, videochip1_1_chipid_out,
       videochip1_1_leftbaty_out, videochip1_1_rightbaty_out, videochip1_2_ballx_out, videochip1_2_bally_out,
       videochip1_2_chipid_out, videochip1_2_leftbaty_out, videochip1_2_rightbaty_out,
       videochip1_3_ballx_out, videochip1_3_bally_out, videochip1_3_chipid_out, videochip1_3_leftbaty_out,
       videochip1_3_rightbaty_out, videochip1_4_ballx_out, videochip1_4_bally_out, videochip1_4_chipid_out,
       videochip1_4_leftbaty_out, videochip1_4_rightbaty_out, videochip1_5_ballx_out, videochip1_5_bally_out,
       videochip1_5_chipid_out, videochip1_5_leftbaty_out, videochip1_5_rightbaty_out,
       videochip1_6_ballx_out, videochip1_6_bally_out, videochip1_6_chipid_out, videochip1_6_leftbaty_out,
       videochip1_6_rightbaty_out, videochip1_7_ballx_out, videochip1_7_bally_out, videochip1_7_chipid_out,
       videochip1_7_leftbaty_out, videochip1_7_rightbaty_out;

  videochip1 videochip1_1 (
    .chipID(chipID), .ballX(ballX), .rightbatY(rightbatY), .columnPattern(columnPattern1),
    .chipID_out(videochip1_1_chipid_out), .rightbatY_out(videochip1_1_rightbaty_out),
    .ballX_out(videochip1_1_ballx_out), .ballY(ballY), .ballY_out(videochip1_1_bally_out),
    .leftbatY(leftbatY), .leftbatY_out(videochip1_1_leftbaty_out));
  videochip1 videochip1_2 (
    .chipID(videochip1_1_chipid_out), .ballX(videochip1_1_ballx_out), .rightbatY(videochip1_1_rightbaty_out),
    .columnPattern(columnPattern2), .chipID_out(videochip1_2_chipid_out),
    .rightbatY_out(videochip1_2_rightbaty_out), .ballX_out(videochip1_2_ballx_out),
    .ballY(videochip1_1_bally_out), .ballY_out(videochip1_2_bally_out), .leftbatY(videochip1_1_leftbaty_out),
    .leftbatY_out(videochip1_2_leftbaty_out));
  videochip1 videochip1_3 (
    .chipID(videochip1_2_chipid_out), .ballX(videochip1_2_ballx_out), .rightbatY(videochip1_2_rightbaty_out),
    .columnPattern(columnPattern3), .chipID_out(videochip1_3_chipid_out),
    .rightbatY_out(videochip1_3_rightbaty_out), .ballX_out(videochip1_3_ballx_out),
    .ballY(videochip1_2_bally_out), .ballY_out(videochip1_3_bally_out), .leftbatY(videochip1_2_leftbaty_out),
    .leftbatY_out(videochip1_3_leftbaty_out));
  videochip1 videochip1_4 (
    .chipID(videochip1_3_chipid_out), .ballX(videochip1_3_ballx_out), .rightbatY(videochip1_3_rightbaty_out),
    .columnPattern(columnPattern4), .chipID_out(videochip1_4_chipid_out),
    .rightbatY_out(videochip1_4_rightbaty_out), .ballX_out(videochip1_4_ballx_out),
    .ballY(videochip1_3_bally_out), .ballY_out(videochip1_4_bally_out), .leftbatY(videochip1_3_leftbaty_out),
    .leftbatY_out(videochip1_4_leftbaty_out));
  videochip1 videochip1_5 (
    .chipID(videochip1_4_chipid_out), .ballX(videochip1_4_ballx_out), .rightbatY(videochip1_4_rightbaty_out),
    .columnPattern(columnPattern5), .chipID_out(videochip1_5_chipid_out),
    .rightbatY_out(videochip1_5_rightbaty_out), .ballX_out(videochip1_5_ballx_out),
    .ballY(videochip1_4_bally_out), .ballY_out(videochip1_5_bally_out), .leftbatY(videochip1_4_leftbaty_out),
    .leftbatY_out(videochip1_5_leftbaty_out));
  videochip1 videochip1_6 (
    .chipID(videochip1_5_chipid_out), .ballX(videochip1_5_ballx_out), .rightbatY(videochip1_5_rightbaty_out),
    .columnPattern(columnPattern6), .chipID_out(videochip1_6_chipid_out),
    .rightbatY_out(videochip1_6_rightbaty_out), .ballX_out(videochip1_6_ballx_out),
    .ballY(videochip1_5_bally_out), .ballY_out(videochip1_6_bally_out), .leftbatY(videochip1_5_leftbaty_out),
    .leftbatY_out(videochip1_6_leftbaty_out));
  videochip1 videochip1_7 (
    .chipID(videochip1_6_chipid_out), .ballX(videochip1_6_ballx_out), .rightbatY(videochip1_6_rightbaty_out),
    .columnPattern(columnPattern7), .chipID_out(videochip1_7_chipid_out),
    .rightbatY_out(videochip1_7_rightbaty_out), .ballX_out(videochip1_7_ballx_out),
    .ballY(videochip1_6_bally_out), .ballY_out(videochip1_7_bally_out), .leftbatY(videochip1_6_leftbaty_out),
    .leftbatY_out(videochip1_7_leftbaty_out));
  videochip1 videochip1_8 (
    .chipID(videochip1_7_chipid_out), .ballX(videochip1_7_ballx_out), .rightbatY(videochip1_7_rightbaty_out),
    .columnPattern(columnPattern8), .chipID_out(chipID_out), .rightbatY_out(rightbatY_out),
    .ballX_out(ballX_out), .ballY(videochip1_7_bally_out), .ballY_out(ballY_out),
    .leftbatY(videochip1_7_leftbaty_out), .leftbatY_out(leftbatY_out));
endmodule

module videochip1 (
  input  [4:0] chipID,
  input  [4:0] ballX,
  input  [4:0] ballY,
  input  [4:0] leftbatY,
  input  [4:0] rightbatY,
  output [4:0] chipID_out,
  output [4:0] ballX_out,
  output [4:0] ballY_out,
  output [4:0] leftbatY_out,
  output [31:0] columnPattern,
  output [4:0] rightbatY_out
);

  wire comparator_1_eq, comparator_2_eq, comparator_3_eq;
  wire [4:0] adder_2_out, adder_3_out, adder_4_out, adder_5_out;
  wire [31:0] decoder_1_out0, decoder_2_out0, decoder_3_out0, decoder_4_out0, decoder_5_out0, decoder_6_out0,
       decoder_7_out0, multiplexer_1_out, or_1_out, or_2_out;

  Comparator #(.width(5)) comparator_1 (.a(chipID), .b(5'b00011), .eq(comparator_1_eq));  // open: gt, lt
  Comparator #(.width(5)) comparator_2 (.a(chipID), .b(5'b11100), .eq(comparator_2_eq));  // open: gt, lt
  Adder #(.width(5)) adder_1 (.a(chipID), .b(5'b00001), .out(chipID_out));  // open: cin, cout
  Comparator #(.width(5)) comparator_3 (.a(chipID), .b(ballX), .eq(comparator_3_eq));  // open: gt, lt
  Decoder #(.select(5), .disabled(0)) decoder_1 (
    .out0(decoder_1_out0[0]), .out1(decoder_1_out0[1]), .out2(decoder_1_out0[2]), .out3(decoder_1_out0[3]),
    .out4(decoder_1_out0[4]), .out5(decoder_1_out0[5]), .out6(decoder_1_out0[6]), .out7(decoder_1_out0[7]),
    .out8(decoder_1_out0[8]), .out9(decoder_1_out0[9]), .out10(decoder_1_out0[10]),
    .out11(decoder_1_out0[11]), .out12(decoder_1_out0[12]), .out13(decoder_1_out0[13]),
    .out14(decoder_1_out0[14]), .out15(decoder_1_out0[15]), .out16(decoder_1_out0[16]),
    .out17(decoder_1_out0[17]), .out18(decoder_1_out0[18]), .out19(decoder_1_out0[19]),
    .out20(decoder_1_out0[20]), .out21(decoder_1_out0[21]), .out22(decoder_1_out0[22]),
    .out23(decoder_1_out0[23]), .out24(decoder_1_out0[24]), .out25(decoder_1_out0[25]),
    .out26(decoder_1_out0[26]), .out27(decoder_1_out0[27]), .out28(decoder_1_out0[28]),
    .out29(decoder_1_out0[29]), .out30(decoder_1_out0[30]), .out31(decoder_1_out0[31]), .sel(leftbatY),
    .en(comparator_1_eq));
  Decoder #(.select(5), .disabled(0)) decoder_2 (
    .out0(decoder_2_out0[0]), .out1(decoder_2_out0[1]), .out2(decoder_2_out0[2]), .out3(decoder_2_out0[3]),
    .out4(decoder_2_out0[4]), .out5(decoder_2_out0[5]), .out6(decoder_2_out0[6]), .out7(decoder_2_out0[7]),
    .out8(decoder_2_out0[8]), .out9(decoder_2_out0[9]), .out10(decoder_2_out0[10]),
    .out11(decoder_2_out0[11]), .out12(decoder_2_out0[12]), .out13(decoder_2_out0[13]),
    .out14(decoder_2_out0[14]), .out15(decoder_2_out0[15]), .out16(decoder_2_out0[16]),
    .out17(decoder_2_out0[17]), .out18(decoder_2_out0[18]), .out19(decoder_2_out0[19]),
    .out20(decoder_2_out0[20]), .out21(decoder_2_out0[21]), .out22(decoder_2_out0[22]),
    .out23(decoder_2_out0[23]), .out24(decoder_2_out0[24]), .out25(decoder_2_out0[25]),
    .out26(decoder_2_out0[26]), .out27(decoder_2_out0[27]), .out28(decoder_2_out0[28]),
    .out29(decoder_2_out0[29]), .out30(decoder_2_out0[30]), .out31(decoder_2_out0[31]), .sel(rightbatY),
    .en(comparator_2_eq));
  Adder #(.width(5)) adder_2 (.a(leftbatY), .b(5'b00001), .out(adder_2_out));  // open: cin, cout
  Adder #(.width(5)) adder_3 (.a(rightbatY), .b(5'b00001), .out(adder_3_out));  // open: cin, cout
  assign or_1_out = decoder_1_out0 | decoder_3_out0 | decoder_5_out0;  // OR_Gate or_1, 32 bits wide
  Decoder #(.select(5), .disabled(0)) decoder_3 (
    .out0(decoder_3_out0[0]), .out1(decoder_3_out0[1]), .out2(decoder_3_out0[2]), .out3(decoder_3_out0[3]),
    .out4(decoder_3_out0[4]), .out5(decoder_3_out0[5]), .out6(decoder_3_out0[6]), .out7(decoder_3_out0[7]),
    .out8(decoder_3_out0[8]), .out9(decoder_3_out0[9]), .out10(decoder_3_out0[10]),
    .out11(decoder_3_out0[11]), .out12(decoder_3_out0[12]), .out13(decoder_3_out0[13]),
    .out14(decoder_3_out0[14]), .out15(decoder_3_out0[15]), .out16(decoder_3_out0[16]),
    .out17(decoder_3_out0[17]), .out18(decoder_3_out0[18]), .out19(decoder_3_out0[19]),
    .out20(decoder_3_out0[20]), .out21(decoder_3_out0[21]), .out22(decoder_3_out0[22]),
    .out23(decoder_3_out0[23]), .out24(decoder_3_out0[24]), .out25(decoder_3_out0[25]),
    .out26(decoder_3_out0[26]), .out27(decoder_3_out0[27]), .out28(decoder_3_out0[28]),
    .out29(decoder_3_out0[29]), .out30(decoder_3_out0[30]), .out31(decoder_3_out0[31]), .sel(adder_2_out),
    .en(comparator_1_eq));
  assign or_2_out = decoder_2_out0 | decoder_4_out0 | decoder_6_out0;  // OR_Gate or_2, 32 bits wide
  Decoder #(.select(5), .disabled(0)) decoder_4 (
    .out0(decoder_4_out0[0]), .out1(decoder_4_out0[1]), .out2(decoder_4_out0[2]), .out3(decoder_4_out0[3]),
    .out4(decoder_4_out0[4]), .out5(decoder_4_out0[5]), .out6(decoder_4_out0[6]), .out7(decoder_4_out0[7]),
    .out8(decoder_4_out0[8]), .out9(decoder_4_out0[9]), .out10(decoder_4_out0[10]),
    .out11(decoder_4_out0[11]), .out12(decoder_4_out0[12]), .out13(decoder_4_out0[13]),
    .out14(decoder_4_out0[14]), .out15(decoder_4_out0[15]), .out16(decoder_4_out0[16]),
    .out17(decoder_4_out0[17]), .out18(decoder_4_out0[18]), .out19(decoder_4_out0[19]),
    .out20(decoder_4_out0[20]), .out21(decoder_4_out0[21]), .out22(decoder_4_out0[22]),
    .out23(decoder_4_out0[23]), .out24(decoder_4_out0[24]), .out25(decoder_4_out0[25]),
    .out26(decoder_4_out0[26]), .out27(decoder_4_out0[27]), .out28(decoder_4_out0[28]),
    .out29(decoder_4_out0[29]), .out30(decoder_4_out0[30]), .out31(decoder_4_out0[31]), .sel(adder_3_out),
    .en(comparator_2_eq));
  Decoder #(.select(5), .disabled(0)) decoder_5 (
    .out0(decoder_5_out0[0]), .out1(decoder_5_out0[1]), .out2(decoder_5_out0[2]), .out3(decoder_5_out0[3]),
    .out4(decoder_5_out0[4]), .out5(decoder_5_out0[5]), .out6(decoder_5_out0[6]), .out7(decoder_5_out0[7]),
    .out8(decoder_5_out0[8]), .out9(decoder_5_out0[9]), .out10(decoder_5_out0[10]),
    .out11(decoder_5_out0[11]), .out12(decoder_5_out0[12]), .out13(decoder_5_out0[13]),
    .out14(decoder_5_out0[14]), .out15(decoder_5_out0[15]), .out16(decoder_5_out0[16]),
    .out17(decoder_5_out0[17]), .out18(decoder_5_out0[18]), .out19(decoder_5_out0[19]),
    .out20(decoder_5_out0[20]), .out21(decoder_5_out0[21]), .out22(decoder_5_out0[22]),
    .out23(decoder_5_out0[23]), .out24(decoder_5_out0[24]), .out25(decoder_5_out0[25]),
    .out26(decoder_5_out0[26]), .out27(decoder_5_out0[27]), .out28(decoder_5_out0[28]),
    .out29(decoder_5_out0[29]), .out30(decoder_5_out0[30]), .out31(decoder_5_out0[31]), .sel(adder_4_out),
    .en(comparator_1_eq));
  Adder #(.width(5)) adder_4 (.a(adder_2_out), .b(5'b00001), .out(adder_4_out));  // open: cin, cout
  Decoder #(.select(5), .disabled(0)) decoder_6 (
    .out0(decoder_6_out0[0]), .out1(decoder_6_out0[1]), .out2(decoder_6_out0[2]), .out3(decoder_6_out0[3]),
    .out4(decoder_6_out0[4]), .out5(decoder_6_out0[5]), .out6(decoder_6_out0[6]), .out7(decoder_6_out0[7]),
    .out8(decoder_6_out0[8]), .out9(decoder_6_out0[9]), .out10(decoder_6_out0[10]),
    .out11(decoder_6_out0[11]), .out12(decoder_6_out0[12]), .out13(decoder_6_out0[13]),
    .out14(decoder_6_out0[14]), .out15(decoder_6_out0[15]), .out16(decoder_6_out0[16]),
    .out17(decoder_6_out0[17]), .out18(decoder_6_out0[18]), .out19(decoder_6_out0[19]),
    .out20(decoder_6_out0[20]), .out21(decoder_6_out0[21]), .out22(decoder_6_out0[22]),
    .out23(decoder_6_out0[23]), .out24(decoder_6_out0[24]), .out25(decoder_6_out0[25]),
    .out26(decoder_6_out0[26]), .out27(decoder_6_out0[27]), .out28(decoder_6_out0[28]),
    .out29(decoder_6_out0[29]), .out30(decoder_6_out0[30]), .out31(decoder_6_out0[31]), .sel(adder_5_out),
    .en(comparator_2_eq));
  Adder #(.width(5)) adder_5 (.a(adder_3_out), .b(5'b00001), .out(adder_5_out));  // open: cin, cout
  Decoder #(.select(5), .enable("false")) decoder_7 (
    .out0(decoder_7_out0[0]), .out1(decoder_7_out0[1]), .out2(decoder_7_out0[2]), .out3(decoder_7_out0[3]),
    .out4(decoder_7_out0[4]), .out5(decoder_7_out0[5]), .out6(decoder_7_out0[6]), .out7(decoder_7_out0[7]),
    .out8(decoder_7_out0[8]), .out9(decoder_7_out0[9]), .out10(decoder_7_out0[10]),
    .out11(decoder_7_out0[11]), .out12(decoder_7_out0[12]), .out13(decoder_7_out0[13]),
    .out14(decoder_7_out0[14]), .out15(decoder_7_out0[15]), .out16(decoder_7_out0[16]),
    .out17(decoder_7_out0[17]), .out18(decoder_7_out0[18]), .out19(decoder_7_out0[19]),
    .out20(decoder_7_out0[20]), .out21(decoder_7_out0[21]), .out22(decoder_7_out0[22]),
    .out23(decoder_7_out0[23]), .out24(decoder_7_out0[24]), .out25(decoder_7_out0[25]),
    .out26(decoder_7_out0[26]), .out27(decoder_7_out0[27]), .out28(decoder_7_out0[28]),
    .out29(decoder_7_out0[29]), .out30(decoder_7_out0[30]), .out31(decoder_7_out0[31]), .sel(ballY));
  Multiplexer #(.width(32)) multiplexer_1 (
    .in0({32{1'b0}}), .in1(decoder_7_out0), .out(multiplexer_1_out), .sel(comparator_3_eq));  // open: en
  assign columnPattern = multiplexer_1_out | or_1_out | or_2_out;  // OR_Gate or_3, 32 bits wide

  assign ballX_out = ballX;
  assign ballY_out = ballY;
  assign leftbatY_out = leftbatY;
  assign rightbatY_out = rightbatY;
endmodule

module controller (
  input  [7:0] rightbatY_CMD_8,
  input  reset,
  input  [4:0] leftbatY,
  input  tick,
  output [4:0] chipID,
  output [4:0] ballX_out,
  output [4:0] ballY_out,
  output [4:0] rightbatY_out,
  output [7:0] scorePerson,
  output [4:0] leftbatY_out,
  output [7:0] scoreRobot,
  output [7:0] ballX_CDM_8,
  output [7:0] ballY_CDM_8,
  output [7:0] speed_CDM_8
);

  wire adder_4_cout, adder_5_cout, adder_12_cout, adder_13_cout, and_1_out, and_4_out, comparator_1_gt,
       comparator_2_gt, comparator_3_gt, comparator_4_eq, comparator_5_eq, comparator_6_eq, comparator_7_eq,
       comparator_8_eq, comparator_9_eq, comparator_10_gt, not_2_out, not_3_out, not_5_out, not_6_out,
       or_1_out, or_2_out, or_3_out, or_4_out, pull_resistor_1_node, upPerson, upRobot, xor_1_out, xor_2_out,
       xor_3_out, xor_4_out, xor_5_out;
  wire [4:0] adder_1_out, adder_6_out, adder_10_out, adder_14_out, multiplexer_1_out, multiplexer_3_out,
       subtractor_1_out;
  wire [7:0] adder_2_out, adder_3_out, adder_5_out, adder_7_out, adder_8_out, adder_9_out, adder_11_out,
       adder_13_out, ballX_8, ballY_8, multiplexer_5_out, multiplexer_6_out, multiplexer_7_out,
       multiplexer_8_out, multiplexer_9_out, multiplexer_10_out, not_1_out, not_4_out, register_2_q,
       register_3_q, speedX, speedY;
  wire [7:3] speedX_out, speedY_out;

  Comparator #(.width(5), .mode("unsigned")) comparator_1 (
    .a(multiplexer_3_out), .b(5'b00001), .gt(comparator_1_gt));  // open: eq, lt
  Subtractor #(.width(5)) subtractor_1 (
    .a(multiplexer_3_out), .b(5'b00001), .out(subtractor_1_out));  // open: bin, bout
  // Probe on rightbatY_CMD_8[7:3]
  Multiplexer #(.width(5), .enable("false")) multiplexer_1 (
    .in0(5'b00001), .in1(subtractor_1_out), .out(multiplexer_1_out), .sel(comparator_1_gt));
  Comparator #(.width(5), .mode("unsigned")) comparator_2 (
    .a(rightbatY_CMD_8[7:3]), .b(5'b11101), .gt(comparator_2_gt));  // open: eq, lt
  // Probe on multiplexer_1_out
  Comparator #(.width(5), .mode("unsigned")) comparator_3 (
    .a(ballX_CDM_8[7:3]), .b(5'b01111), .gt(comparator_3_gt));  // open: eq, lt
  Adder #(.width(5)) adder_1 (.a(5'b00001), .b(leftbatY_out), .out(adder_1_out));  // open: cin, cout
  Comparator #(.width(5)) comparator_4 (.a(leftbatY_out), .b(ballY_CDM_8[7:3]), .eq(comparator_4_eq));  // open: gt, lt
  Adder adder_2 (.a(ballX_8), .b(8'he4), .out(adder_2_out));  // open: cin, cout
  xor xor_1 (xor_1_out, speedX[7], adder_5_cout);
  Multiplexer #(.width(8), .enable("false")) multiplexer_2 (
    .in0(speedX), .in1(adder_3_out), .out({speedX_out, speed_CDM_8[2:0]}), .sel(or_2_out));
  assign not_1_out = ~speedX;  // NOT_Gate not_1, 8 bits wide
  Adder adder_3 (.a(not_1_out), .b(8'h1), .out(adder_3_out));  // open: cin, cout
  Multiplexer #(.width(5), .enable("false")) multiplexer_3 (
    .in0(rightbatY_CMD_8[7:3]), .in1(5'b11101), .out(multiplexer_3_out), .sel(comparator_2_gt));
  Register #(.width(5)) register_1 (
    .D(multiplexer_1_out), .en(not_2_out), .Q(rightbatY_out), .clk(or_3_out));  // open: clr
  not not_2 (not_2_out, comparator_3_gt);
  // Probe on scorePerson
  // Probe on scoreRobot
  // Probe on ballX_CDM_8
  // Probe on ballY_CDM_8
  Comparator #(.width(5)) comparator_5 (.a(adder_1_out), .b(ballY_CDM_8[7:3]), .eq(comparator_5_eq));  // open: gt, lt
  or or_1 (or_1_out, comparator_4_eq, comparator_5_eq, comparator_6_eq);
  Adder adder_4 (.a(adder_2_out), .b(speedX), .cout(adder_4_cout));  // open: out, cin
  xor xor_2 (xor_2_out, speedX[7], adder_4_cout);
  and and_1 (and_1_out, xor_2_out, or_1_out);
  Adder adder_5 (.a(ballX_8), .b(speedX), .out(adder_5_out), .cout(adder_5_cout));  // open: cin
  or or_2 (or_2_out, xor_1_out, and_1_out, and_4_out);
  // Probe on {speedX_out, speed_CDM_8[2:0]}
  // Probe on {speedY_out, speed_CDM_8[5:3]}
  Adder #(.width(5)) adder_6 (.a(5'b00001), .b(adder_1_out), .out(adder_6_out));  // open: cin, cout
  Comparator #(.width(5)) comparator_6 (.a(adder_6_out), .b(ballY_CDM_8[7:3]), .eq(comparator_6_eq));  // open: gt, lt
  Multiplexer #(.width(8), .enable("false")) multiplexer_4 (
    .in0(adder_5_out), .in1(ballX_8), .out(ballX_CDM_8), .sel(or_2_out));
  Multiplexer #(.width(8), .enable("false")) multiplexer_5 (
    .in0(scorePerson), .in1({8{1'b0}}), .out(multiplexer_5_out), .sel(reset));
  Multiplexer #(.width(8), .enable("false")) multiplexer_6 (
    .in0(scoreRobot), .in1({8{1'b0}}), .out(multiplexer_6_out), .sel(reset));
  Multiplexer #(.width(8), .enable("false")) multiplexer_7 (
    .in0(ballX_CDM_8), .in1(8'h80), .out(multiplexer_7_out), .sel(reset));
  Multiplexer #(.width(8), .enable("false")) multiplexer_8 (
    .in0(ballY_CDM_8), .in1(8'h80), .out(multiplexer_8_out), .sel(reset));
  Multiplexer #(.width(8), .enable("false")) multiplexer_9 (
    .in0({speedX_out, speed_CDM_8[2:0]}), .in1(8'hfe), .out(multiplexer_9_out), .sel(reset));
  Multiplexer #(.width(8), .enable("false")) multiplexer_10 (
    .in0({speedY_out, speed_CDM_8[5:3]}), .in1(8'hfe), .out(multiplexer_10_out), .sel(reset));
  and and_2 (upPerson, xor_1_out, adder_3_out[7]);
  not not_3 (not_3_out, adder_3_out[7]);
  and and_3 (upRobot, not_3_out, xor_1_out);
  Register register_2 (.D(multiplexer_5_out), .en(1'b1), .Q(register_2_q), .clk(or_3_out));  // open: clr
  Register register_3 (.D(multiplexer_6_out), .en(1'b1), .Q(register_3_q), .clk(or_3_out));  // open: clr
  Register #(.trigger("falling")) register_4 (
    .D(multiplexer_7_out), .en(1'b1), .Q(ballX_8), .clk(or_3_out));  // open: clr
  Register #(.trigger("falling")) register_5 (
    .D(multiplexer_8_out), .en(1'b1), .Q(ballY_8), .clk(or_3_out));  // open: clr
  Register register_6 (.D(multiplexer_9_out), .en(1'b1), .Q(speedX), .clk(or_3_out));  // open: clr
  Register register_7 (.D(multiplexer_10_out), .en(1'b1), .Q(speedY), .clk(or_3_out));  // open: clr
  Comparator #(.width(5)) comparator_7 (.a(rightbatY_out), .b(ballY_CDM_8[7:3]), .eq(comparator_7_eq));  // open: gt, lt
  xor xor_3 (xor_3_out, speedY[7], adder_13_cout);
  assign not_4_out = ~speedY;  // NOT_Gate not_4, 8 bits wide
  Adder adder_7 (.a(not_4_out), .b(8'h1), .out(adder_7_out));  // open: cin, cout
  Multiplexer #(.width(8), .enable("false")) multiplexer_11 (
    .in0(register_2_q), .in1(adder_8_out), .out(scorePerson), .sel(upPerson));
  Adder adder_8 (.a(register_2_q), .b(8'h1), .out(adder_8_out));  // open: cin, cout
  Multiplexer #(.width(8), .enable("false")) multiplexer_12 (
    .in0(register_3_q), .in1(adder_9_out), .out(scoreRobot), .sel(upRobot));
  Adder adder_9 (.a(register_3_q), .b(8'h1), .out(adder_9_out));  // open: cin, cout
  Adder #(.width(5)) adder_10 (.a(5'b00001), .b(rightbatY_out), .out(adder_10_out));  // open: cin, cout
  Comparator #(.width(5)) comparator_8 (.a(adder_10_out), .b(ballY_CDM_8[7:3]), .eq(comparator_8_eq));  // open: gt, lt
  Adder adder_11 (.a(ballX_8), .b(8'h1c), .out(adder_11_out));  // open: cin, cout
  Adder adder_12 (.a(adder_11_out), .b(speedX), .cout(adder_12_cout));  // open: out, cin
  xor xor_4 (xor_4_out, speedX[7], adder_12_cout);
  and and_4 (and_4_out, xor_4_out, or_4_out);
  Adder adder_13 (.a(ballY_8), .b(speedY), .out(adder_13_out), .cout(adder_13_cout));  // open: cin
  Multiplexer #(.width(8), .enable("false")) multiplexer_13 (
    .in0(speedY), .in1(adder_7_out), .out({speedY_out, speed_CDM_8[5:3]}), .sel(xor_3_out));
  or or_3 (or_3_out, xor_5_out, pull_resistor_1_node);
  xor xor_5 (xor_5_out, reset, not_5_out);
  not not_5 (not_5_out, not_6_out);
  not not_6 (not_6_out, reset);
  Adder #(.width(5)) adder_14 (.a(5'b00001), .b(adder_10_out), .out(adder_14_out));  // open: cin, cout
  or or_4 (or_4_out, comparator_7_eq, comparator_8_eq, comparator_9_eq);
  Pull_Resistor pull_resistor_1 (.node(pull_resistor_1_node));
  Transistor transistor_1 (.in(tick), .out(pull_resistor_1_node), .gate(reset));
  Comparator #(.width(5)) comparator_9 (.a(adder_14_out), .b(ballY_CDM_8[7:3]), .eq(comparator_9_eq));  // open: gt, lt
  Multiplexer #(.width(8), .enable("false")) multiplexer_14 (
    .in0(adder_13_out), .in1(ballY_8), .out(ballY_CDM_8), .sel(xor_3_out));
  Comparator #(.width(5), .mode("unsigned")) comparator_10 (
    .a(leftbatY), .b(5'b11101), .gt(comparator_10_gt));  // open: eq, lt
  Multiplexer #(.width(5), .enable("false")) multiplexer_15 (
    .in0(leftbatY), .in1(5'b11101), .out(leftbatY_out), .sel(comparator_10_gt));

  assign ballX_out = ballX_CDM_8[7:3];
  assign ballY_out = ballY_CDM_8[7:3];
  assign chipID = {5{1'b0}};
  assign speed_CDM_8[7:6] = 2'b00;

  // Other names for the same wires on the sheet: ballX_5[4:0] = ballX_CDM_8[7:3]; ballX_8_out[7:0] = ballX_CDM_8;
  //   ballY_5[4:0] = ballY_CDM_8[7:3]; ballY_8_out[7:0] = ballY_CDM_8; leftbatY_t[4:0] = leftbatY_out;
  //   rightbatY[4:0] = rightbatY_out; speedX_out[2:0] = speed_CDM_8[2:0]; speedY_out[2:0] = speed_CDM_8[5:3]

  // Notes on the sheet:
  //   ballX
  //   7 bit speedX
  //   speedX
  //   rightbat
  //   speedX
  //   leftbat
  //   ballX
  //   7 bit speedX
endmodule

module calcScore (
  input  [7:0] in,
  output [3:0] tens,
  output [3:0] ones
);

  wire [7:0] divider_1_out, divider_1_rem;

  Divider divider_1 (.a(in), .b(8'ha), .out(divider_1_out), .rem(divider_1_rem));  // open: upper
  Bit_Extender #(.out_width(4)) bit_extender_1 (.in(divider_1_out), .out(tens));
  Bit_Extender #(.out_width(4)) bit_extender_2 (.in(divider_1_rem), .out(ones));
endmodule

module processor (
  input  [7:0] ballX,
  input  [7:0] ballY,
  input  [7:0] speed,
  output [7:0] rightbatY
);

  wire and_3_out, and_6_out, and_8_out, and_10_out, button_1_out, cdm_8_mark5_1_p1, cdm_8_mark5_1_p2,
       cdm_8_mark5_1_p4, cdm_8_mark5_1_p5, cdm_8_mark5_1_p6, cdm_8_mark5_1_p7, cdm_8_mark5_1_p8, cl, code,
       data, goBat, goS, goX, goY, I_O_sel, mem, nand_1_out, not_1_out, not_2_out, not_3_out, not_4_out,
       r_wr_prime, RAM;
  wire [3:0] I_O_adr;
  wire [7:0] cdm_8_mark5_1_p12, cdm_8_mark5_1_p13, I_O_dat;
  wire [7:4] cdm_8_mark5_1_p11;

  // Probe on cdm_8_mark5_1_p5
  // Probe on cdm_8_mark5_1_p2
  // Probe on cdm_8_mark5_1_p4
  // Probe on cdm_8_mark5_1_p1
  Clock clock_1 (.out(cl));
  and and_1 (I_O_sel, not_2_out, cl, data);
  and and_2 (goX, r_wr_prime, I_O_sel, and_3_out);
  and and_3 (and_3_out, I_O_adr[0], I_O_adr[1], ~I_O_adr[2], ~I_O_adr[3]);  // AND_Gate
  // Probe on cdm_8_mark5_1_p6
  // Probe on cdm_8_mark5_1_p7
  // CdM_8_mark5 cdm_8_mark5_1: pin names not known; wires that end beside it: cdm_8_mark5_1_p1, cdm_8_mark5_1_p2, cl, cdm_8_mark5_1_p4, cdm_8_mark5_1_p5, cdm_8_mark5_1_p6, cdm_8_mark5_1_p7, cdm_8_mark5_1_p8, mem, r_wr_prime, {cdm_8_mark5_1_p11, I_O_adr}, cdm_8_mark5_1_p12, cdm_8_mark5_1_p13
  Decoder #(.disabled(0)) decoder_1 (.out0(code), .out1(data), .sel(cdm_8_mark5_1_p8), .en(mem));
  assign I_O_dat = not_1_out ? cdm_8_mark5_1_p12 : 8'bz;  // Controlled_Buffer controlled_buffer_1
  not not_1 (not_1_out, r_wr_prime);
  assign cdm_8_mark5_1_p13 = r_wr_prime ? I_O_dat : 8'bz;  // Controlled_Buffer controlled_buffer_2
  not not_2 (not_2_out, nand_1_out);
  and and_4 (RAM, nand_1_out, data);
  nand nand_1 (nand_1_out, cdm_8_mark5_1_p11[4], cdm_8_mark5_1_p11[5], cdm_8_mark5_1_p11[6], cdm_8_mark5_1_p11[7]);
  and and_5 (goY, r_wr_prime, I_O_sel, and_6_out);
  and and_6 (and_6_out, ~I_O_adr[0], ~I_O_adr[1], I_O_adr[2], ~I_O_adr[3]);  // AND_Gate
  // Probe on {cdm_8_mark5_1_p11, I_O_adr}
  ROM rom_1 (.addr({cdm_8_mark5_1_p11, I_O_adr}), .data(I_O_dat), .sel(code));
  RAM ram_1 (
    .addr({cdm_8_mark5_1_p11, I_O_adr}), .data(I_O_dat), .sel(RAM), .clk(cl), .ld(r_wr_prime),
    .clr(button_1_out));
  Button button_1 (.out(button_1_out));
  and and_7 (goS, r_wr_prime, I_O_sel, and_8_out);
  and and_8 (and_8_out, I_O_adr[0], ~I_O_adr[1], I_O_adr[2], ~I_O_adr[3]);  // AND_Gate
  // Probe on I_O_dat
  Register register_1 (.D(I_O_dat), .Q(rightbatY), .clk(goBat));  // open: en, clr
  assign I_O_dat = goX ? ballX : 8'bz;  // Controlled_Buffer controlled_buffer_3
  assign I_O_dat = goY ? ballY : 8'bz;  // Controlled_Buffer controlled_buffer_4
  assign I_O_dat = goS ? speed : 8'bz;  // Controlled_Buffer controlled_buffer_5
  not not_3 (not_3_out, r_wr_prime);
  and and_9 (goBat, not_3_out, not_4_out, cl, and_10_out);
  // Probe on ballX
  // Probe on ballY
  // Probe on speed
  not not_4 (not_4_out, I_O_sel);
  and and_10 (and_10_out, I_O_adr[0], I_O_adr[1], ~I_O_adr[2], ~I_O_adr[3]);  // AND_Gate

  // Other names for the same wires on the sheet: toBat[7:0] = I_O_dat

  // Notes on the sheet:
  //   contents of rom_1 (hex, n*v repeats v):
  //   cd ef d0 1 0 e0 b8 d0 f5 b0 d1 4 41 e1 b6 d2 f3 ba d1 78 76 e8 b6 d2 f3 ba d1 e0 36 1 d3 7 4d d3 38
  //   4c 98 98 98 d3 4 43 e0 2f d3 f8 5c d3 1 77 e0 56 d3 2 77 e1 3f 9a d3 7f 4e ee 56 c0 d0 0 95 79 e9 4c
  //   8c 7 3b e ee 43 d3 2 3b 2 1a f e4 55 8e c4 d3 4 43 e0 5f d1 ff ee 61 d1 1 c2 71 e0 7e d3 4 43 e0 6d
  //   89 ee 6e 8d c7 c3 1e e3 7c c0 d3 b9 bf 8f d0 b9 a3 c4 ee 62 c7 d3 4 43 e0 85 86 d3 4 43 e0 96 d0 f4
  //   b0 12 d3 b9 bf e2 94 8f ee a0 d0 f4 b0 12 d3 b9 bf e3 a0 8f d0 1 4c e0 a6 86 d0 f3 b0 d1 78 74 e4 b1
  //   d0 f3 a2 d0 0 d1 b9 a4 ee 2 d4
endmodule
